// Logisim project inicio.circ as structural Verilog: 1 circuit, main circuit main
module main (
);

  wire clock_1_out;

  Clock clock_1 (.out(clock_1_out));
  D_Flip_Flop d_ff_1 (.clk(clock_1_out));  // open: D, Q, Qn, preset, en, reset
  D_Flip_Flop d_ff_2 (.clk(clock_1_out));  // open: D, Q, Qn, preset, en, reset
  D_Flip_Flop d_ff_3 (.clk(clock_1_out));  // open: D, Q, Qn, preset, en, reset
  D_Flip_Flop d_ff_4 (.clk(clock_1_out));  // open: D, Q, Qn, preset, en, reset
  _7_Segment_Display u_7_segment_display_1 ();  // open: g, f, a, b, e, d, c, dp
endmodule
